// Logisim project s-mips.circ as structural Verilog: 24 circuits, main circuit S-MIPS Board
module S_MIPS_Board (
  input  DESHABILITAR_DISPATCHER,
  output halt
);

  wire button_1_out, CLK, CS, d_ff_1_q, LCLR, LoadRAM, LoadRAMOn, LW, R_R_W, R_W, ram_dispatcher_1_finished,
       RCS, Reset_out, RST, TTY_EN;
  wire [2:0] KDB;
  wire [3:0] LMask, Mask, ram_1_read_time, ram_1_write_time, RMask;
  wire [6:0] KDB_DATA, TTY_DATA;
  wire [15:0] Addr, LAddr, RAddr;
  wire [31:0] I0, I1, I2, I3, LData, ram_1_data_out_0, ram_1_data_out_1, ram_1_data_out_2, ram_1_data_out_3,
       RI0, RI1, RI2, RI3;

  TTY #(.rows(25), .cols(80)) tty_1 (.data(TTY_DATA), .clk(CLK), .we(TTY_EN), .clr(RST));
  not not_1 (LoadRAMOn, ram_dispatcher_1_finished);
  RAM_Dispatcher ram_dispatcher_1 (
    .WriteTime(ram_1_write_time), .Clock(CLK), .Data(LData), .Address(LAddr), .Mask(LMask),
    .Finished(ram_dispatcher_1_finished), .Write(LW), .CLR(LCLR));
  Keyboard #(.buflen(64)) keyboard_1 (.clk(CLK), .re(KDB[0]), .avail(KDB[2]), .data(KDB_DATA));  // open: clr
  RAM ram_1 (
    .Address(RAddr), .Data_Out_0(ram_1_data_out_0), .Data_Out_1(ram_1_data_out_1),
    .Data_Out_2(ram_1_data_out_2), .Data_Out_3(ram_1_data_out_3), .Data_In_0(RI0), .Data_In_1(RI1),
    .Data_In_2(RI2), .Data_In_3(RI3), .Mask(RMask), .nRead_Write(R_R_W), .Chip_Select(RCS),
    .Read_Time(ram_1_read_time), .Reset(button_1_out), .Write_Time(ram_1_write_time));
  Button button_1 (.out(button_1_out));
  D_Flip_Flop d_ff_1 (.clk(CLK), .D(1'b1), .Q(d_ff_1_q), .reset(Reset_out));  // open: Qn, preset, en
  Button Reset (.out(Reset_out));
  S_MIPS s_mips_1 (
    .Kbd_Enable(KDB[0]), .Address(Addr), .Kbd_Clear(KDB[1]), .Kbd_Available(KDB[2]), .RAM_In_0(I0),
    .Kbd_ASCII_Data(KDB_DATA), .RAM_In_1(I1), .TTY_Enable(TTY_EN), .RAM_In_2(I2), .RAM_In_3(I3),
    .TTY_ASCII_Data(TTY_DATA), .Reset(RST), .RAM_Out_0(ram_1_data_out_0), .Clock(CLK),
    .RAM_Out_1(ram_1_data_out_1), .Stop(halt), .RAM_Out_2(ram_1_data_out_2), .RAM_Out_3(ram_1_data_out_3),
    .Mask(Mask), .Read_Time(ram_1_read_time), .Write_Time(ram_1_write_time), .nRead_Write(R_W),
    .Chip_Select(CS));
  D_Flip_Flop d_ff_2 (.clk(CLK), .D(d_ff_1_q), .Qn(LCLR), .reset(Reset_out));  // open: Q, preset, en
  or or_1 (RST, LCLR, LoadRAM);
  Clock clock_1 (.out(CLK));
  Multiplexer #(.width(32), .enable("false")) multiplexer_1 (.in0(I0), .in1(LData), .out(RI0), .sel(LoadRAM));
  Multiplexer #(.width(32), .enable("false")) multiplexer_2 (.in0(I1), .in1(LData), .out(RI1), .sel(LoadRAM));
  Multiplexer #(.width(32), .enable("false")) multiplexer_3 (.in0(I2), .in1(LData), .out(RI2), .sel(LoadRAM));
  Multiplexer #(.width(32), .enable("false")) multiplexer_4 (.in0(I3), .in1(LData), .out(RI3), .sel(LoadRAM));
  and and_1 (LoadRAM, ~DESHABILITAR_DISPATCHER, LoadRAMOn);  // AND_Gate
  Multiplexer #(.width(16), .enable("false")) multiplexer_5 (.in0(Addr), .in1(LAddr), .out(RAddr), .sel(LoadRAM));
  Multiplexer #(.width(4), .enable("false")) multiplexer_6 (.in0(Mask), .in1(LMask), .out(RMask), .sel(LoadRAM));
  Multiplexer #(.enable("false")) multiplexer_7 (.in0(CS), .in1(LW), .out(RCS), .sel(LoadRAM));
  Multiplexer #(.enable("false")) multiplexer_8 (.in0(R_W), .in1(LW), .out(R_R_W), .sel(LoadRAM));

  // Notes on the sheet:
  //   NO MODIFICAR
  //   Keyboard
endmodule

module RAM (
  input  [15:0] Address,
  input  [31:0] Data_In_0,
  input  [31:0] Data_In_1,
  input  [31:0] Data_In_2,
  input  [31:0] Data_In_3,
  input  [3:0] Mask,
  input  nRead_Write,
  input  Chip_Select,
  input  Reset,
  output [31:0] Data_Out_0,
  output [31:0] Data_Out_1,
  output [31:0] Data_Out_2,
  output [31:0] Data_Out_3,
  output [3:0] Read_Time,
  output [3:0] Write_Time
);

  wire and_2_out, and_3_out, and_4_out, and_5_out, and_6_out, and_7_out, and_8_out, and_9_out, Changed, CLK,
       comparator_2_eq, comparator_3_eq, comparator_4_eq, comparator_5_eq, comparator_6_eq, Count,
       demultiplexer_3_out0, Idle, Idle_q, Load, Load0, Load1, nand_1_out, or_1_out, or_2_out, or_3_out,
       or_4_out, or_5_out, or_6_out, or_7_out, or_8_out, or_9_out, or_10_out, Proc_q, Update_Mem, Zero_Time;
  wire [3:0] counter_1_q, multiplexer_1_out, subtractor_1_out;
  wire [31:0] register_1_q, register_2_q, register_3_q, register_4_q, register_5_q;

  // Probe on 4'b0011
  // Probe on 4'b0010
  Multiplexer #(.width(4), .enable("false")) multiplexer_1 (
    .in0(4'b0011), .in1(4'b0010), .out(multiplexer_1_out), .sel(nRead_Write));
  or or_1 (or_1_out, Idle, Update_Mem);
  or or_2 (or_2_out, ~Chip_Select, Reset);  // OR_Gate
  Subtractor #(.width(4)) subtractor_1 (.a(multiplexer_1_out), .b(4'b0010), .out(subtractor_1_out));  // open: bin, bout
  Demultiplexer #(.enable("false")) demultiplexer_1 (.out0(Idle), .out1(Load0), .in(Idle_q), .sel(Changed));
  D_Flip_Flop u_Idle (.clk(CLK), .D(or_1_out), .Q(Idle_q), .preset(or_2_out));  // open: Qn, en, reset
  // Probe on counter_1_q
  Counter #(.width(4), .max('hf)) counter_1 (
    .load(Load), .D(subtractor_1_out), .count(Count), .Q(counter_1_q), .clk(CLK), .clr(or_3_out));  // open: carry
  or or_3 (or_3_out, ~Chip_Select, Reset);  // OR_Gate
  Comparator #(.width(4), .mode("unsigned")) comparator_1 (
    .a(4'b0000), .b(counter_1_q), .eq(Zero_Time));  // open: gt, lt
  or or_4 (or_4_out, Count, Load0, Load1);
  Register #(.width(32)) register_1 (.D(Data_In_0), .en(Chip_Select), .Q(register_1_q), .clk(CLK), .clr(or_5_out));
  or or_5 (or_5_out, ~Chip_Select, Reset);  // OR_Gate
  Register #(.width(32)) register_2 (.D(Data_In_1), .en(Chip_Select), .Q(register_2_q), .clk(CLK), .clr(or_6_out));
  or or_6 (or_6_out, ~Chip_Select, Reset);  // OR_Gate
  Register #(.width(32)) register_3 (.D(Data_In_2), .en(Chip_Select), .Q(register_3_q), .clk(CLK), .clr(or_7_out));
  or or_7 (or_7_out, ~Chip_Select, Reset);  // OR_Gate
  Register #(.width(32)) register_4 (.D(Data_In_3), .en(Chip_Select), .Q(register_4_q), .clk(CLK), .clr(or_8_out));
  or or_8 (or_8_out, ~Chip_Select, Reset);  // OR_Gate
  Register #(.width(32)) register_5 (
    .D({{11{1'b1}}, nRead_Write, Mask, Address}), .en(Chip_Select), .Q(register_5_q), .clk(CLK),
    .clr(or_9_out));
  or or_9 (or_9_out, ~Chip_Select, Reset);  // OR_Gate
  D_Flip_Flop Proc (.clk(CLK), .D(or_4_out), .Q(Proc_q), .reset(or_10_out));  // open: Qn, preset, en
  or or_10 (or_10_out, ~Chip_Select, Reset);  // OR_Gate
  Demultiplexer #(.enable("false")) demultiplexer_2 (
    .out0(Count), .out1(Update_Mem), .in(demultiplexer_3_out0), .sel(Zero_Time));
  Demultiplexer #(.enable("false")) demultiplexer_3 (
    .out0(demultiplexer_3_out0), .out1(Load1), .in(Proc_q), .sel(Changed));
  Clock clock_1 (.out(CLK));
  Comparator #(.width(32)) comparator_2 (.a(register_1_q), .b(Data_In_0), .eq(comparator_2_eq));  // open: gt, lt
  Comparator #(.width(32)) comparator_3 (.a(register_2_q), .b(Data_In_1), .eq(comparator_3_eq));  // open: gt, lt
  Comparator #(.width(32)) comparator_4 (.a(register_3_q), .b(Data_In_2), .eq(comparator_4_eq));  // open: gt, lt
  Comparator #(.width(32)) comparator_5 (.a(register_4_q), .b(Data_In_3), .eq(comparator_5_eq));  // open: gt, lt
  Comparator #(.width(32)) comparator_6 (
    .a(register_5_q), .b({{11{1'b1}}, nRead_Write, Mask, Address}), .eq(comparator_6_eq));  // open: gt, lt
  nand nand_1 (nand_1_out, comparator_6_eq, comparator_2_eq, comparator_3_eq, comparator_4_eq, comparator_5_eq);
  and and_1 (Changed, nand_1_out, Chip_Select);
  or or_11 (Load, Count, Load1, Load0);
  and and_2 (and_2_out, Mask[0], Update_Mem, nRead_Write);
  and and_3 (and_3_out, Mask[1], Update_Mem, nRead_Write);
  and and_4 (and_4_out, Mask[2], Update_Mem, nRead_Write);
  and and_5 (and_5_out, Mask[3], Update_Mem, nRead_Write);
  RAM_part #(.addrWidth(16), .dataWidth(32), .bus("separate")) ram_1 (
    .addr(Address), .din(Data_In_0), .data(Data_Out_0), .str(and_2_out), .sel(Chip_Select), .clk(CLK),
    .ld(and_6_out), .clr(Reset));
  and and_6 (and_6_out, ~nRead_Write, Idle);  // AND_Gate
  RAM_part #(.addrWidth(16), .dataWidth(32), .bus("separate")) ram_2 (
    .addr(Address), .din(Data_In_1), .data(Data_Out_1), .str(and_3_out), .sel(Chip_Select), .clk(CLK),
    .ld(and_7_out), .clr(Reset));
  and and_7 (and_7_out, ~nRead_Write, Idle);  // AND_Gate
  RAM_part #(.addrWidth(16), .dataWidth(32), .bus("separate")) ram_3 (
    .addr(Address), .din(Data_In_2), .data(Data_Out_2), .str(and_4_out), .sel(Chip_Select), .clk(CLK),
    .ld(and_8_out), .clr(Reset));
  and and_8 (and_8_out, ~nRead_Write, Idle);  // AND_Gate
  RAM_part #(.addrWidth(16), .dataWidth(32), .bus("separate")) ram_4 (
    .addr(Address), .din(Data_In_3), .data(Data_Out_3), .str(and_5_out), .sel(Chip_Select), .clk(CLK),
    .ld(and_9_out), .clr(Reset));
  and and_9 (and_9_out, ~nRead_Write, Idle);  // AND_Gate

  assign Read_Time = 4'b0011;
  assign Write_Time = 4'b0010;

  // Other names for the same wires on the sheet: M0 = Mask[0]; M1 = Mask[1]; M2 = Mask[2]; M3 = Mask[3];
  //   RW = nRead_Write; CLR = Reset; CS = Chip_Select; Load2 = Count

  // Notes on the sheet:
  //   NO MODIFICAR
  //   excepto quizás los valores RT y WT
  //   BANK0
  //   BANK1
  //   BANK2
  //   BANK3
endmodule

module S_MIPS (
  input  Kbd_Available,
  input  [6:0] Kbd_ASCII_Data,
  input  [31:0] RAM_Out_0,
  input  [31:0] RAM_Out_1,
  input  Reset,
  input  [31:0] RAM_Out_2,
  input  Clock,
  input  [31:0] RAM_Out_3,
  input  [3:0] Read_Time,
  input  [3:0] Write_Time,
  output Kbd_Enable,
  output [15:0] Address,
  output Kbd_Clear,
  output TTY_Enable,
  output [6:0] TTY_ASCII_Data,
  output Stop,
  output [31:0] RAM_In_0,
  output [31:0] RAM_In_1,
  output [31:0] RAM_In_2,
  output [31:0] RAM_In_3,
  output [3:0] Mask,
  output nRead_Write,
  output Chip_Select
);


  // Other names for the same wires on the sheet: CLK = Clock; CLR = Reset; CS = Chip_Select;
  //   KBD_AVAIL = Kbd_Available; KBD_CLR = Kbd_Clear; KBD_DATA[6:0] = Kbd_ASCII_Data; RAM_A[15:0] = Address;
  //   RAM_INPUT_0[31:0] = RAM_In_0; RAM_INPUT_1[31:0] = RAM_In_1; RAM_INPUT_2[31:0] = RAM_In_2;
  //   RAM_INPUT_3[31:0] = RAM_In_3; RAM_MASK[3:0] = Mask; RAM_OUTPUT_0[31:0] = RAM_Out_0;
  //   RAM_OUTPUT_1[31:0] = RAM_Out_1; RAM_OUTPUT_2[31:0] = RAM_Out_2; RAM_OUTPUT_3[31:0] = RAM_Out_3;
  //   RW = nRead_Write; TTY_DATA[6:0] = TTY_ASCII_Data

  // Notes on the sheet:
  //   RAM ADDRESS
  //   DATA FROM RAM
  //   DATA TO RAM
  //   DATA WRITE MASK
  //   RAM TIMING
  //   RAM CONTROL
  //   KEYBOARD
  //   TTY
  //   SEQUENCING
endmodule

module RAM_Dispatcher (
  input  [3:0] WriteTime,
  input  Clock,
  input  CLR,
  output [31:0] Data,
  output [15:0] Address,
  output [3:0] Mask,
  output Finished,
  output Write
);

  wire demultiplexer_2_out1, demultiplexer_3_out1, End, IDLE_q, IncAddr, Load, or_1_out, or_2_out, While_q,
       WriteEnd;
  wire [3:0] counter_1_q;
  wire [31:0] CurrentAddress_q;

  Counter #(.width(32), .max('hffffffff)) CurrentAddress (
    .count(IncAddr), .Q({CurrentAddress_q[31:18], Address, CurrentAddress_q[1:0]}), .clk(Clock), .clr(CLR));  // open: load, D, carry
  or or_1 (or_1_out, IncAddr, demultiplexer_3_out1, Finished);
  D_Flip_Flop IDLE (.clk(Clock), .D(or_1_out), .Q(IDLE_q), .preset(CLR));  // open: Qn, en, reset
  Demultiplexer #(.enable("false")) demultiplexer_1 (.out0(Load), .out1(Finished), .in(IDLE_q), .sel(End));
  D_Flip_Flop While (.clk(Clock), .D(or_2_out), .Q(While_q), .reset(CLR));  // open: Qn, preset, en
  or or_2 (or_2_out, Write, Load);
  RAM_part #(.addrWidth(18), .dataWidth(32)) ram_1 (
    .addr({Address, CurrentAddress_q[1:0]}), .data(Data), .clk(Clock));  // open: sel, ld, clr
  Demultiplexer #(.enable("false")) demultiplexer_2 (
    .out0(Write), .out1(demultiplexer_2_out1), .in(While_q), .sel(WriteEnd));
  Decoder #(.select(2)) decoder_1 (
    .out0(Mask[0]), .out1(Mask[1]), .out2(Mask[2]), .out3(Mask[3]), .sel(CurrentAddress_q[1:0]));  // open: en
  Demultiplexer #(.enable("false")) demultiplexer_3 (
    .out0(IncAddr), .out1(demultiplexer_3_out1), .in(demultiplexer_2_out1), .sel(End));
  Counter #(.width(4), .max('hf)) counter_1 (
    .load(Load), .D(WriteTime), .count(Write), .Q(counter_1_q), .clk(Clock));  // open: carry, clr
  Comparator #(.width(32)) comparator_1 (.a(Data), .b({32{1'b1}}), .eq(End));  // open: gt, lt
  Comparator #(.width(4)) comparator_2 (.a(4'b0000), .b(counter_1_q), .eq(WriteEnd));  // open: gt, lt

  // Other names for the same wires on the sheet: CLK = Clock; Count = Write; WT[3:0] = WriteTime
endmodule

module Register_File (
  input  [31:0] Di,
  input  [4:0] Da,
  input  Rw,
  input  [4:0] Sa,
  input  [4:0] Sb,
  input  Whl,
  input  [31:0] IHi,
  input  [31:0] Ilow,
  input  Clock,
  input  Rst,
  input  [31:0] in_11,
  input  in_12,
  output [31:0] A,
  output [31:0] B,
  output [31:0] Hi,
  output [31:0] Low,
  output [31:0] SP
);

  wire Ld00, Ld01, Ld02, Ld03, Ld04, Ld05, Ld06, Ld07, Ld08, Ld09, Ld10, Ld11, Ld12, Ld13, Ld14, Ld15, Ld16,
       Ld17, Ld18, Ld19, Ld20, Ld21, Ld22, Ld23, Ld24, Ld25, Ld26, Ld27, Ld28, Ld29, Ld30;
  wire [31:0] R00, R01, R02, R03, R04, R05, R06, R07, R08, R09, R10, R11, R12, R13, R14, R15, R16, R17, R18,
       R19, R20, R21, R22, R23, R24, R25, R26, R27, R28, R29, R30, undriven, undriven_2;

  Demultiplexer #(.select(5), .enable("false")) demultiplexer_1 (
    .out0(Ld00), .out1(Ld01), .out2(Ld02), .out3(Ld03), .out4(Ld04), .out5(Ld05), .out6(Ld06), .out7(Ld07),
    .out8(Ld08), .out9(Ld09), .out10(Ld10), .out11(Ld11), .out12(Ld12), .out13(Ld13), .out14(Ld14),
    .out15(Ld15), .out16(Ld16), .out17(Ld17), .out18(Ld18), .out19(Ld19), .out20(Ld20), .out21(Ld21),
    .out22(Ld22), .out23(Ld23), .out24(Ld24), .out25(Ld25), .out26(Ld26), .out27(Ld27), .out28(Ld28),
    .out29(Ld29), .out30(Ld30), .in(Rw), .sel(Da));  // open: out31
  Register #(.width(32)) u_R00 (.en(Ld00), .Q(R00), .clk(Clock), .clr(Rst));  // open: D
  Register #(.width(32)) u_R01 (.en(Ld01), .Q(R01), .clk(Clock), .clr(Rst));  // open: D
  Register #(.width(32)) u_R02 (.en(Ld02), .Q(R02), .clk(Clock), .clr(Rst));  // open: D
  Register #(.width(32)) u_R03 (.en(Ld03), .Q(R03), .clk(Clock), .clr(Rst));  // open: D
  Register #(.width(32)) u_R04 (.en(Ld04), .Q(R04), .clk(Clock), .clr(Rst));  // open: D
  Register #(.width(32)) u_R05 (.en(Ld05), .Q(R05), .clk(Clock), .clr(Rst));  // open: D
  Register #(.width(32)) u_R06 (.en(Ld06), .Q(R06), .clk(Clock), .clr(Rst));  // open: D
  Register #(.width(32)) u_R07 (.en(Ld07), .Q(R07), .clk(Clock), .clr(Rst));  // open: D
  Register #(.width(32)) u_R08 (.en(Ld08), .Q(R08), .clk(Clock), .clr(Rst));  // open: D
  Register #(.width(32)) u_R09 (.en(Ld09), .Q(R09), .clk(Clock), .clr(Rst));  // open: D
  Register #(.width(32)) u_R10 (.en(Ld10), .Q(R10), .clk(Clock), .clr(Rst));  // open: D
  Register #(.width(32)) u_R11 (.en(Ld11), .Q(R11), .clk(Clock), .clr(Rst));  // open: D
  Register #(.width(32)) u_R12 (.en(Ld12), .Q(R12), .clk(Clock), .clr(Rst));  // open: D
  Register #(.width(32)) u_R13 (.en(Ld13), .Q(R13), .clk(Clock), .clr(Rst));  // open: D
  Register #(.width(32)) u_R14 (.en(Ld14), .Q(R14), .clk(Clock), .clr(Rst));  // open: D
  Register #(.width(32)) u_R15 (.en(Ld15), .Q(R15), .clk(Clock), .clr(Rst));  // open: D
  Register #(.width(32)) u_R16 (.en(Ld16), .Q(R16), .clk(Clock), .clr(Rst));  // open: D
  Register #(.width(32)) u_R17 (.en(Ld17), .Q(R17), .clk(Clock), .clr(Rst));  // open: D
  Register #(.width(32)) u_R18 (.en(Ld18), .Q(R18), .clk(Clock), .clr(Rst));  // open: D
  Register #(.width(32)) u_R19 (.en(Ld19), .Q(R19), .clk(Clock), .clr(Rst));  // open: D
  Register #(.width(32)) u_R20 (.en(Ld20), .Q(R20), .clk(Clock), .clr(Rst));  // open: D
  Register #(.width(32)) u_R21 (.en(Ld21), .Q(R21), .clk(Clock), .clr(Rst));  // open: D
  Register #(.width(32)) u_R22 (.en(Ld22), .Q(R22), .clk(Clock), .clr(Rst));  // open: D
  Register #(.width(32)) u_R23 (.en(Ld23), .Q(R23), .clk(Clock), .clr(Rst));  // open: D
  Register #(.width(32)) u_R24 (.en(Ld24), .Q(R24), .clk(Clock), .clr(Rst));  // open: D
  Register #(.width(32)) u_R25 (.en(Ld25), .Q(R25), .clk(Clock), .clr(Rst));  // open: D
  Register #(.width(32)) u_R26 (.en(Ld26), .Q(R26), .clk(Clock), .clr(Rst));  // open: D
  Register #(.width(32)) u_R27 (.en(Ld27), .Q(R27), .clk(Clock), .clr(Rst));  // open: D
  Register #(.width(32)) u_R28 (.en(Ld28), .Q(R28), .clk(Clock), .clr(Rst));  // open: D
  Register #(.width(32)) u_R29 (.en(Ld29), .Q(R29), .clk(Clock), .clr(Rst));  // open: D
  Register #(.width(32)) u_R30 (.en(Ld30), .Q(R30), .clk(Clock), .clr(Rst));  // open: D
  Register #(.width(32)) R31 (.en(in_12), .Q(SP), .clk(Clock), .clr(Rst));  // open: D
  Register #(.width(32)) RHi (.en(Whl), .Q(Hi), .clk(Clock), .clr(Rst));  // open: D
  Register #(.width(32)) Rlow (.en(Whl), .Q(Low), .clk(Clock), .clr(Rst));  // open: D
  Multiplexer #(.select(5), .width(32), .enable("false")) multiplexer_1 (
    .in0(R00), .in1(R01), .in2(R02), .in3(R03), .in4(R04), .in5(undriven), .in6(R06), .in7(R07), .in8(R08),
    .in9(R09), .in10(R10), .in11(R11), .in12(R12), .in13(R13), .in14(R14), .in15(R15), .in16(R16),
    .in17(R17), .in18(R18), .in19(R19), .in20(R20), .in21(R21), .in22(R22), .in23(R23), .in24(R24),
    .in25(R25), .in26(R26), .in27(R27), .in28(R28), .in29(R29), .in30(R30), .out(A), .sel(Sa));  // open: in31
  Multiplexer #(.select(5), .width(32), .enable("false")) multiplexer_2 (
    .in0(R00), .in1(R01), .in2(R02), .in3(R03), .in4(R04), .in5(undriven_2), .in6(R06), .in7(R07), .in8(R08),
    .in9(R09), .in10(R10), .in11(R11), .in12(R12), .in13(R13), .in14(R14), .in15(R15), .in16(R16),
    .in17(R17), .in18(R18), .in19(R19), .in20(R20), .in21(R21), .in22(R22), .in23(R23), .in24(R24),
    .in25(R25), .in26(R26), .in27(R27), .in28(R28), .in29(R29), .in30(R30), .out(B), .sel(Sb));  // open: in31

  // Other names for the same wires on the sheet: Clk = Clock; In_Sp[31:0] = in_11; Ld_SP = in_12; RHi[31:0] = Hi;
  //   Rlow[31:0] = Low

  // Notes on the sheet:
  //   Sa: pull=down
endmodule

module Div_Signed (
  input  [31:0] x,
  input  [31:0] y,
  output [31:0] DivRem,
  output [31:0] Div
);

  wire SignX, SignY, xor_1_out;
  wire [31:0] adder_1_out, Div_t, multiplexer_4_out, negator_1_out, negator_2_out, negator_3_out, Rem,
       subtractor_1_out, X1, Y1;

  Subtractor #(.width(32)) subtractor_1 (.a(Y1), .b(Rem), .out(subtractor_1_out));  // open: bin, bout
  Multiplexer #(.width(32)) multiplexer_1 (.in0(Rem), .in1(subtractor_1_out), .out(DivRem), .sel(SignX));  // open: en
  Sign_Getter sign_getter_1 (.in_1(x), .Output(SignX));
  Sign_Getter sign_getter_2 (.in_1(y), .Output(SignY));
  Negator #(.width(32)) negator_1 (.in(x), .out(negator_1_out));
  Negator #(.width(32)) negator_2 (.in(y), .out(negator_2_out));
  Multiplexer #(.width(32), .enable("false")) multiplexer_2 (.in0(x), .in1(negator_1_out), .out(X1), .sel(SignX));
  Multiplexer #(.width(32), .enable("false")) multiplexer_3 (.in0(y), .in1(negator_2_out), .out(Y1), .sel(SignY));
  Divider #(.width(32)) divider_1 (.a(X1), .b(Y1), .out(Div_t), .rem(Rem));  // open: upper
  Adder #(.width(32)) adder_1 (.a(Div_t), .b(32'h1), .out(adder_1_out));  // open: cin, cout
  Multiplexer #(.width(32), .enable("false")) multiplexer_4 (
    .in0(Div_t), .in1(adder_1_out), .out(multiplexer_4_out), .sel(SignX));
  Negator #(.width(32)) negator_3 (.in(multiplexer_4_out), .out(negator_3_out));
  Multiplexer #(.width(32), .enable("false")) multiplexer_5 (
    .in0(multiplexer_4_out), .in1(negator_3_out), .out(Div), .sel(xor_1_out));
  xor xor_1 (xor_1_out, SignY, SignX);

  // Other names for the same wires on the sheet: OH[31:0] = DivRem; OL[31:0] = Div
endmodule

module Sign_Getter (
  input  [31:0] in_1,
  output Output
);


  assign Output = in_1[31];
endmodule

module Mul_signed (
  input  [31:0] In1,
  input  [31:0] In2,
  output [31:0] Lo,
  output [31:0] Hi
);

  wire adder_1_cout, adder_3_cout;
  wire [15:0] mix1_high, mix1_low, mix2_high, mix2_low;
  wire [31:0] adder_1_out, adder_2_out, bit_extender_1_out, bit_extender_2_out, prehigh, prelower, value_1_0,
       value_1_1, value_2_0, value_2_1;

  assign bit_extender_1_out = {{16{1'b0}}, mix1_high};  // Bit_Extender bit_extender_1
  assign bit_extender_2_out = {{16{1'b0}}, mix2_high};  // Bit_Extender bit_extender_2
  assign value_1_0 = {{16{1'b0}}, In1[15:0]};  // Bit_Extender bit_extender_3
  assign value_1_1 = {{16{1'b0}}, In1[31:16]};  // Bit_Extender bit_extender_4
  assign value_2_0 = {{16{1'b0}}, In2[15:0]};  // Bit_Extender bit_extender_5
  assign value_2_1 = {{16{1'b0}}, In2[31:16]};  // Bit_Extender bit_extender_6
  Adder #(.width(32)) adder_1 (
    .a({mix1_low, {16{1'b0}}}), .b({mix2_low, {16{1'b0}}}), .out(adder_1_out), .cout(adder_1_cout));  // open: cin
  Adder #(.width(32)) adder_2 (
    .a(bit_extender_1_out), .b(bit_extender_2_out), .out(adder_2_out), .cin(adder_1_cout));  // open: cout
  Adder #(.width(32)) adder_3 (.a(prelower), .b(adder_1_out), .out(Lo), .cout(adder_3_cout));  // open: cin
  Adder #(.width(32)) adder_4 (.a(prehigh), .b(adder_2_out), .out(Hi), .cin(adder_3_cout));  // open: cout
  Multiplier #(.width(32)) multiplier_1 (.a(value_1_0), .b(value_2_0), .out(prelower));  // open: cin, cout
  Multiplier #(.width(32)) multiplier_2 (.a(value_1_0), .b(value_2_1), .out({mix1_high, mix1_low}));  // open: cin, cout
  Multiplier #(.width(32)) multiplier_3 (.a(value_1_1), .b(value_2_0), .out({mix2_high, mix2_low}));  // open: cin, cout
  Multiplier #(.width(32)) multiplier_4 (.a(value_1_1), .b(value_2_1), .out(prehigh));  // open: cin, cout
endmodule

module Comparer (
  input  [31:0] in_1,
  input  [31:0] in_2,
  output [31:0] Out
);

  wire comparator_1_lt;

  Comparator #(.width(32)) comparator_1 (.a(in_1), .b(in_2), .lt(comparator_1_lt));  // open: gt, eq
  Multiplexer #(.width(32), .enable("false")) multiplexer_1 (
    .in0(32'h1), .in1({32{1'b0}}), .out(Out), .sel(comparator_1_lt));
endmodule

module ComparerUnsigned (
  input  [31:0] in_1,
  input  [31:0] in_2,
  output [31:0] Out
);

  wire comparator_1_lt;

  Comparator #(.width(32), .mode("unsigned")) comparator_1 (.a(in_1), .b(in_2), .lt(comparator_1_lt));  // open: gt, eq
  Multiplexer #(.width(32), .enable("false")) multiplexer_1 (
    .in0(32'h1), .in1({32{1'b0}}), .out(Out), .sel(comparator_1_lt));
endmodule

module ALU (
  input  [3:0] in_1,
  input  [31:0] in_2,
  input  [31:0] in_3,
  input  [31:0] Result,
  output [31:0] highOut,
  output [31:0] lowOut,
  output Gf,
  output Ef,
  output Lf
);

  wire addc, comparator_2_lt, subc;
  wire [31:0] add, \and , divHi, divLo, divuHi, divuLo, mulHi, mulLo, muluHi, muluLo, \nor , \or , Result_t,
       SlT, SlTU, sub, \xor ;

  Comparator #(.width(32), .mode("unsigned")) comparator_1 (.a(in_2), .b(in_3), .gt(Gf), .eq(Ef), .lt(Lf));
  assign \and  = in_2 & in_3;  // AND_Gate and_1, 32 bits wide
  assign \or  = in_2 | in_3;  // OR_Gate or_1, 32 bits wide
  assign \nor  = ~(in_2 | in_3);  // NOR_Gate nor_1, 32 bits wide
  assign \xor  = in_2 ^ in_3;  // XOR_Gate xor_1, 32 bits wide
  Mul_signed mul_signed_1 (.In1(in_2), .In2(in_3), .Lo(mulLo), .Hi(mulHi));
  Div_Signed div_signed_1 (.x(in_2), .y(in_3), .DivRem(divLo), .Div(divHi));
  Adder #(.width(32)) adder_1 (.a(in_2), .b(in_3), .out(add), .cout(addc));  // open: cin
  Subtractor #(.width(32)) subtractor_1 (.a(in_2), .b(in_3), .out(sub), .bout(subc));  // open: bin
  Multiplier #(.width(32)) multiplier_1 (.a(in_2), .b(in_3), .out(muluLo), .cout(muluHi));  // open: cin
  Divider #(.width(32)) divider_1 (.a(in_2), .b(in_3), .out(divuLo), .rem(divuHi));  // open: upper
  assign SlTU = {{31{1'b0}}, Lf};  // Bit_Extender bit_extender_1
  Comparator #(.width(32)) comparator_2 (.a(in_2), .b(in_3), .lt(comparator_2_lt));  // open: gt, eq
  assign SlT = {{31{1'b0}}, comparator_2_lt};  // Bit_Extender bit_extender_2
  // Probe on in_1[1:0]
  Multiplexer #(.select(2), .width(32)) multiplexer_1 (
    .in0(muluLo), .in1(mulLo), .in2(divuLo), .in3(divLo), .out(highOut), .sel(in_1[1:0]), .en(in_1[3]));
  Multiplexer #(.select(2), .width(32)) multiplexer_2 (
    .in0(muluLo), .in1(mulLo), .in2(divuLo), .in3(divLo), .out(lowOut), .sel(in_1[1:0]), .en(in_1[3]));
  Multiplexer #(.select(3), .width(32), .enable("false")) multiplexer_3 (
    .in0(add), .in1(sub), .in2(\and ), .in3(\or ), .in4(\nor ), .in5(\xor ), .in6(SlT), .in7(SlTU),
    .out(Result_t), .sel(in_1[2:0]));
  // Probe on in_1[2:0]

  // Other names for the same wires on the sheet: A[31:0] = in_2; B[31:0] = in_3; Hio[31:0] = highOut;
  //   Lwo[31:0] = lowOut; S1[2:0] = in_1[2:0]; S2[1:0] = in_1[1:0]; selectGeneral[3:0] = in_1; MDOP = in_1[3]

  // Notes on the sheet:
  //   Imputs
  //   Logic Operations
  //   Arithmetic Logic Unity
  //   Arithmetic Operations
  //   Comparison Operations
endmodule

module ZeroFlag (
  input  [31:0] IN,
  output ZF
);

  nor nor_1 (ZF, IN[0], IN[1], IN[2], IN[3], IN[4], IN[5], IN[6], IN[7], IN[8], IN[9], IN[10], IN[11], IN[12], IN[13], IN[14], IN[15], IN[16], IN[17], IN[18], IN[19], IN[20], IN[21], IN[22], IN[23], IN[24], IN[25], IN[26], IN[27], IN[28], IN[29], IN[30], IN[31]);
endmodule

module DataPath (
  input  [1:0] in_1,
  input  [3:0] in_2,
  input  in_3,
  input  in_4,
  input  in_5,
  input  in_6,
  input  [31:0] in_7,
  input  [2:0] in_8,
  input  [1:0] in_9,
  input  in_10,
  input  [2:0] in_11,
  input  in_12,
  input  in_13,
  input  [31:0] in_14,
  input  [1:0] in_15,
  input  in_16,
  input  in_17,
  input  in_18,
  input  [1:0] in_19,
  output [31:0] Address,
  output [5:0] Fun_Code,
  output [5:0] Op,
  output [31:0] Data
);

  wire Ef, Gf, instruction_decoder_memory_1_p11, Lf, Zf;
  wire [4:0] Da, RD, Rs, RT;
  wire [15:0] OffSet, OfSet;
  wire [25:0] Destiny;
  wire [31:0] A, Alu_HI, Alu_Lo, Alu_Result, B, branch_control_1_output, Di, Hi, Inm_Sign, Inm_Zero, Lo,
       multiplexer_5_out, multiplexer_6_out, Pc, Random, Sp;

  Branch_Control branch_control_1 (
    .in_1(Destiny), .in_2(Pc), .in_3(in_9), .in_4(Ef), .in_5(Gf), .in_6(Lf), .in_8(OfSet), .in_9(A),
    .Output(branch_control_1_output), .in_7(in_11));
  Random #(.width(32)) random_1 (.clk(in_4), .next(1'b1), .out(Random));  // open: clr
  assign Inm_Zero = {{16{1'b0}}, OffSet};  // Bit_Extender bit_extender_1
  assign Inm_Sign = {{16{OffSet[15]}}, OffSet};  // Bit_Extender bit_extender_2
  Multiplexer #(.width(5), .enable("false")) multiplexer_1 (.in0(RD), .in1(RT), .out(Da), .sel(in_12));
  Multiplexer #(.select(3), .width(32), .enable("false")) multiplexer_2 (
    .in0(Alu_Result), .in1(Hi), .in2(Lo), .in3(in_7), .in4(Random), .out(Di), .sel(in_8));  // open: in5, in6, in7
  Register #(.width(32)) u_PC (.D(branch_control_1_output), .en(in_10), .Q(Pc), .clk(in_4));  // open: clr
  // Instruction_Decoder_Memory instruction_decoder_memory_1: pin names not known; wires that end beside it: in_14, in_13, in_4, Fun_Code, RD, RT, Rs, Op, Destiny, OffSet, instruction_decoder_memory_1_p11
  Multiplexer #(.width(32), .enable("false")) multiplexer_3 (.in0(A), .in1(B), .out(Data), .sel(in_16));
  Multiplexer #(.select(2), .width(32), .enable("false")) multiplexer_4 (
    .in0(Alu_Result), .in1(Pc), .in2(A), .in3(Sp), .out(Address), .sel(in_15));
  Register_File register_file_1 (
    .A(A), .Di(Di), .B(B), .Da(Da), .Rw(in_5), .Sa(Rs), .Sb(RT), .Whl(in_3), .IHi(Alu_HI), .Ilow(Alu_Lo),
    .Clock(in_4), .Rst(in_6), .Hi(Hi), .Low(Lo), .SP(Sp), .in_11(Alu_Result), .in_12(in_17));
  Multiplexer #(.width(32), .enable("false")) multiplexer_5 (.in0(A), .in1(Sp), .out(multiplexer_5_out), .sel(in_18));
  Multiplexer #(.select(2), .width(32), .enable("false")) multiplexer_6 (
    .in0(B), .in1(32'h4), .in2(Inm_Zero), .in3(Inm_Sign), .out(multiplexer_6_out), .sel(in_19));
  // ALU alu_1: pin names not known; wires that end beside it: multiplexer_5_out, multiplexer_6_out, Zf, in_2, Gf, Ef, Lf, Alu_Result, Alu_HI, Alu_Lo

  // Other names for the same wires on the sheet: Address_Sel[1:0] = in_15; BranchSel[2:0] = in_11; Clk = in_4;
  //   Da_Sel = in_12; Data_from_ram[31:0] = in_7; Data_Sel = in_16; Di_selector[2:0] = in_8; Fc[5:0] = Fun_Code;
  //   Instruction[31:0] = in_14; Instruction_Register_LD = in_13; LD_PC = in_10; LD_SP = in_17;
  //   Operand_Selector[1:0] = in_1; Operand_Selector_A = in_18; Operand_Selector_B[1:0] = in_19;
  //   Operation_Selector[3:0] = in_2; Pc_Sel[1:0] = in_9; RST_RF = in_6; WRF = in_5; Write_Hi_Lo = in_3

  // Notes on the sheet:
  //   Inputs
  //   Auxiliary OP
  //   Outputs
endmodule

module Branch_Control (
  input  [25:0] in_1,
  input  [31:0] in_2,
  input  [1:0] in_3,
  input  in_4,
  input  in_5,
  input  in_6,
  input  [2:0] in_7,
  input  [15:0] in_8,
  input  [31:0] in_9,
  output [31:0] Output
);

  wire Branch, not_1_out, not_2_out;
  wire [31:0] adder_2_out, multiplexer_2_out, OfSet, PC___4, shifter_1_out;

  assign OfSet = {{16{1'b0}}, in_8};  // Bit_Extender bit_extender_1
  not not_1 (not_1_out, in_4);
  not not_2 (not_2_out, in_5);
  Adder #(.width(32)) adder_1 (.a(in_2), .b(32'h4), .out(PC___4));  // open: cin, cout
  Shifter #(.width(32)) shifter_1 (.in(OfSet), .\dist (5'b00010), .out(shifter_1_out));
  Adder #(.width(32)) adder_2 (.a(PC___4), .b(shifter_1_out), .out(adder_2_out));  // open: cin, cout
  Multiplexer #(.select(3), .enable("false")) multiplexer_1 (
    .in0(in_4), .in1(not_1_out), .in2(in_5), .in3(not_2_out), .in4(in_6), .out(Branch), .sel(in_7));  // open: in5, in6, in7
  Multiplexer #(.width(32), .enable("false")) multiplexer_2 (
    .in0(PC___4), .in1(adder_2_out), .out(multiplexer_2_out), .sel(Branch));
  Multiplexer #(.select(2), .width(32), .enable("false")) multiplexer_3 (
    .in0(PC___4), .in1(multiplexer_2_out), .in2({in_2[31:28], in_1, 2'b00}), .in3(in_9), .out(Output),
    .sel(in_3));

  // Other names for the same wires on the sheet: Alu_Ef = in_4; Alu_Gf = in_5; Alu_Lf = in_6;
  //   Branch_Selector[2:0] = in_7; Destiny[25:0] = in_1; Jump_Value[31:2] = {in_2[31:28], in_1}; Pc[31:0] = in_2;
  //   Pc_prime[31:0] = Output; Pc_Selector[1:0] = in_3; Rs[31:0] = in_9
endmodule

module Instruction_Decoder_Memory (
  input  [5:0] in_1,
  input  [5:0] in_2,
  output nop,
  output add,
  output sub,
  output mult,
  output mulu,
  output div,
  output divu,
  output slt,
  output sltu,
  output \and ,
  output \or ,
  output \xor ,
  output \nor ,
  output pop,
  output push,
  output mfhi,
  output mflo,
  output jr,
  output addi,
  output sltiu,
  output slti,
  output ori,
  output andi,
  output xori,
  output lw,
  output sw,
  output beq,
  output bne,
  output blez,
  output bgtz,
  output bltz,
  output J,
  output halt,
  output tty,
  output rnd,
  output kbd
);

  wire _00, _01, _10, _11, and_10_out, and_11_out, and_25_out, and_26_out, and_27_out, and_34_out,
       and_41_out, and_46_out, comparator_1_eq, Especial, I, or_1_out, R, R_00, R_01, R_10;

  and and_1 (_10, ~in_1[0], I, in_1[1]);  // AND_Gate
  and and_2 (_11, in_1[0], I, in_1[1]);
  and and_3 (_01, in_1[0], I, ~in_1[1]);  // AND_Gate
  and and_4 (_00, ~in_1[0], I, ~in_1[1]);  // AND_Gate
  and and_5 (addi, ~in_1[2], _00, in_1[3]);  // AND_Gate
  and and_6 (andi, in_1[2], _00, in_1[3]);
  and and_7 (beq, in_1[2], _00, ~in_1[3]);  // AND_Gate
  and and_8 (mflo, ~in_2[3], R_01, in_2[1]);  // AND_Gate
  and and_9 (mfhi, ~in_2[3], R_01, ~in_2[1]);  // AND_Gate
  and and_10 (and_10_out, in_2[3], R_01, ~in_2[1]);  // AND_Gate
  and and_11 (and_11_out, in_2[3], R_01, in_2[1]);
  and and_12 (mulu, and_10_out, in_2[0]);
  and and_13 (divu, and_11_out, in_2[0]);
  and and_14 (div, and_11_out, ~in_2[0]);  // AND_Gate
  and and_15 (mult, and_10_out, ~in_2[0]);  // AND_Gate
  and and_16 (slti, ~in_1[2], _10, in_1[3]);  // AND_Gate
  and and_17 (xori, in_1[2], _10, in_1[3]);
  and and_18 (blez, in_1[2], _10, ~in_1[3]);  // AND_Gate
  and and_19 (R_00, ~in_2[4], R, ~in_2[5]);  // AND_Gate
  and and_20 (R_10, ~in_2[4], R, in_2[5]);  // AND_Gate
  and and_21 (R_01, in_2[4], R, ~in_2[5]);  // AND_Gate
  and and_22 (bne, in_1[2], _01, ~in_1[3]);  // AND_Gate
  and and_23 (ori, in_1[2], _01, in_1[3]);
  and and_24 (bltz, ~in_1[2], _01, ~in_1[3]);  // AND_Gate
  and and_25 (and_25_out, ~in_2[3], R_10, ~in_2[2]);  // AND_Gate
  and and_26 (and_26_out, in_2[3], R_10, in_2[1]);
  and and_27 (and_27_out, ~in_2[3], R_10, in_2[2]);  // AND_Gate
  and and_28 (\xor , in_2[3], R_10, ~in_2[1]);  // AND_Gate
  and and_29 (sub, in_2[1], and_25_out);
  and and_30 (add, ~in_2[1], and_25_out);  // AND_Gate
  and and_31 (sltu, and_26_out, in_2[0]);
  and and_32 (slt, ~in_2[0], and_26_out);  // AND_Gate
  and and_33 (\and , and_27_out, ~in_2[0]);  // AND_Gate
  and and_34 (and_34_out, and_27_out, in_2[0]);
  and and_35 (\nor , and_34_out, in_2[1]);
  and and_36 (\or , ~in_2[1], and_34_out);  // AND_Gate
  and and_37 (sltiu, ~in_1[5], _11, in_1[3]);  // AND_Gate
  and and_38 (sw, in_1[5], _11, in_1[3]);
  and and_39 (lw, in_1[5], _11, ~in_1[3]);  // AND_Gate
  and and_40 (bgtz, ~in_1[5], _11, ~in_1[3]);  // AND_Gate
  Comparator #(.width(6)) comparator_1 (.a(in_1), .b({6{1'b0}}), .eq(comparator_1_eq));  // open: gt, lt
  or or_1 (or_1_out, comparator_1_eq, and_41_out);
  and and_41 (and_41_out, in_1[5], in_1[4], in_1[3]);
  Comparator #(.width(6)) comparator_2 (.a(in_1), .b(6'b000010), .eq(J));  // open: gt, lt
  and and_42 (Especial, and_41_out, in_1[2]);
  and and_43 (I, ~or_1_out, ~J);  // AND_Gate
  and and_44 (jr, ~in_2[0], R_00, in_2[3]);  // AND_Gate
  and and_45 (push, in_2[0], R_00, ~in_2[3]);  // AND_Gate
  and and_46 (and_46_out, ~in_2[0], R_00, ~in_2[3]);  // AND_Gate
  and and_47 (R, or_1_out, ~Especial);  // AND_Gate
  and and_48 (halt, in_2[0], Especial, in_2[1]);
  and and_49 (tty, in_2[0], Especial, ~in_2[1]);  // AND_Gate
  and and_50 (rnd, ~in_2[0], Especial, in_2[1]);  // AND_Gate
  and and_51 (kbd, ~in_2[0], Especial, ~in_2[1]);  // AND_Gate
  and and_52 (pop, and_46_out, in_1[5]);
  and and_53 (nop, and_46_out, ~in_1[5]);  // AND_Gate

  // Other names for the same wires on the sheet: F_bit1 = in_2[0]; FuncCode[5:0] = in_2; F_bit2 = in_2[1];
  //   F_bit3 = in_2[2]; F_bit4 = in_2[3]; mvhi = mfhi; mvlo = mflo; OpCode[5:0] = in_1; Bit3 = in_1[2];
  //   Bit4 = in_1[3]; Bit6 = in_1[5]
endmodule

// End8
module Control_Unit (
  input  [5:0] in_1,
  input  [5:0] in_2,
  input  in_3,
  input  in_4,
  input  in_5,
  output DA_Sel,
  output [1:0] PC_Sel,
  output UseRam,
  output [2:0] Branch_Sel,
  output [2:0] Di_Sel,
  output WriteRam,
  output [1:0] Addres_Sel,
  output Halt,
  output tty_En,
  output WRF,
  output [3:0] operation_sel,
  output Data_Sel,
  output WHi_Lo,
  output operand_A_sel,
  output WSP,
  output LD_IR,
  output KBD_En,
  output [1:0] operand_B_sel,
  output LD_PC
);

  wire add, addi, \and , and_1_out, and_2_out, and_3_out, and_4_out, and_5_out, and_6_out, and_7_out, andi,
       beq, bgtz, blez, bltz, bne, demultiplexer_1_out0, demultiplexer_1_out1, demultiplexer_3_out1, div,
       divu, En_Ram, En_Ram1, En_Ram2, En_Ram3, En_Ram4, End1, End2, End3, End4, End5, End6, End7, End8,
       End9, EXCECUTE, EXECUTE, EXECUTED, EXECUTING_q, IDLE_q, J, j_t, jr, kbd, Ld_Pc1, Ld_Pc2, Ld_Pc2_t,
       Ld_Pc3, Ld_Pc4, Ld_Pc5, Ld_Pc6, Ld_Pc7, Ld_Pc8, Ld_Pc9, lw, mul, mult, mulu, mvhi, mvlo, nop, \nor ,
       operand_A_sel_1, operand_A_sel_2, \or , or_1_out, or_2_out, or_6_out, pop, push, READING_q,
       RESET_EXECUTERS, rnd, slt, slti, sltiu, sltu, sub, sw, Type_AL, Type_Al_t, Type_Branch, Type_Hi_Lo,
       Type_Inm, Type_Inm_t, Type_Special, W_RF2, WRF1, WRF2, WRF3, WRF4, WRF5, WRF6, WSp1, WSp2, \xor , xori;
  wire [1:0] ADDR_Sel, ADDR_Sel1, ADDR_Sel2, operand_B_SEL1, operand_B_sel_1, operand_B_sel_2,
       operand_B_sel_3, operand_B_sel_4, operand_B_sel_5, or_18_out;
  wire [2:0] Di_Sel1, Di_Sel2, Di_Sel3, Di_Sel4;
  wire [3:0] op_sel_1, op_sel_2, op_sel_2_t, op_sel_3;

  and and_1 (and_1_out, pop, EXECUTE);
  D_Flip_Flop #(.trigger("falling")) IDLE (
    .clk(in_3), .D(demultiplexer_1_out0), .Q(IDLE_q), .preset(in_5));  // open: Qn, en, reset
  Demultiplexer #(.enable("false")) demultiplexer_1 (
    .out0(demultiplexer_1_out0), .out1(demultiplexer_1_out1), .in(IDLE_q), .sel(in_5));
  and and_2 (and_2_out, Type_Al_t, EXECUTE);
  Type_Inmediate type_inmediate_1 (
    .in_1(addi), .in_2(andi), .in_3(andi), .in_4(xori), .in_5(slti), .in_6(sltiu), .in_7(and_3_out),
    .operand_sel(op_sel_2), .Operand_B(operand_B_sel_1), .WRF(WRF2), .\end (End2), .Pc_LD(Ld_Pc2));
  and and_3 (and_3_out, EXECUTE, Type_Inm);
  Pop pop_1 (
    .in_1(in_4), .in_2(and_1_out), .in_3(RESET_EXECUTERS), .in_4(in_3), .Operand_B_Sel(En_Ram1),
    .Operand_A_Sel(ADDR_Sel1), .Output(operand_A_sel_1), .Output_2(WRF3), .Output_3(WSp1), .Output_4(Ld_Pc3),
    .out_7(operand_B_sel_5), .out_12(Di_Sel1), .Output_5(End3));
  Multiplexer #(.width(2), .enable("false")) multiplexer_1 (.in0(2'b00), .in1(2'b01), .out(ADDR_Sel), .sel(En_Ram));
  or or_1 (or_1_out, En_Ram, demultiplexer_1_out1, demultiplexer_3_out1);
  Type_AL type_al_1 (
    .in_1(add), .in_2(sub), .in_3(mul), .in_4(mulu), .in_5(div), .in_6(divu), .in_7(\and ), .in_8(\or ),
    .in_9(\nor ), .in_10(\xor ), .in_11(slt), .in_12(sltu), .Operation_Sel(op_sel_1), .WRF(WRF1),
    .WH_L(WHi_Lo), .LD_PC(Ld_Pc1), .in_13(and_2_out), .End(End1));
  D_Flip_Flop #(.trigger("falling")) READING (.clk(in_3), .D(or_1_out), .Q(READING_q));  // open: Qn, preset, en, reset
  Demultiplexer #(.enable("false")) demultiplexer_2 (.out0(En_Ram), .out1(LD_IR), .in(READING_q), .sel(in_4));
  Instruction_Decoder_Memory instruction_decoder_memory_1 (
    .nop(nop), .in_1(in_1), .add(add), .sub(sub), .in_2(in_2), .mult(mult), .mulu(mulu), .div(div),
    .divu(divu), .slt(slt), .sltu(sltu), .\and (\and ), .\or (\or ), .\xor (\xor ), .\nor (\nor ), .pop(pop),
    .push(push), .mfhi(mvhi), .mflo(mvlo), .jr(jr), .addi(addi), .sltiu(sltiu), .slti(slt), .ori(andi),
    .andi(andi), .xori(xori), .lw(lw), .sw(sw), .beq(beq), .bne(bne), .blez(blez), .bgtz(bgtz), .bltz(bltz),
    .J(j_t), .halt(Halt), .tty(tty_En), .rnd(rnd), .kbd(kbd));
  and and_4 (and_4_out, EXECUTE, Type_Branch);
  or or_2 (or_2_out, EXECUTE, LD_IR);
  and and_5 (and_5_out, Type_Hi_Lo, EXECUTE);
  and and_6 (and_6_out, EXECUTE, push);
  Branch_Operations branch_operations_1 (
    .in_1(beq), .in_2(bne), .in_3(blez), .in_4(bgtz), .in_5(bltz), .in_6(J), .in_7(jr), .in_9(and_4_out),
    .Branch_sel(Branch_Sel), .Pc_Sel(PC_Sel), .Ld_PC(Ld_Pc8), .\end (End8), .in_8(nop));
  D_Flip_Flop #(.trigger("falling")) EXECUTING (
    .clk(in_3), .D(or_2_out), .Q(EXECUTING_q));  // open: Qn, preset, en, reset
  Type_H_L type_h_l_1 (
    .in_1(mvhi), .in_2(mvlo), .in_3(and_5_out), .wrf(WRF4), .LD_PC(Ld_Pc4), .Di_Sel(Di_Sel2), .\end (End4));
  Demultiplexer #(.enable("false")) demultiplexer_3 (
    .out0(EXECUTE), .out1(demultiplexer_3_out1), .in(EXECUTING_q), .sel(EXECUTED));
  // PUSH push_1: pin names not known; wires that end beside it: and_6_out, LD_IR, in_3, in_4, WriteRam, En_Ram2, ADDR_Sel2, Di_Sel4, operand_A_sel_2, operand_B_sel_2, op_sel_3, WSp2, Ld_Pc9, End9
  or or_3 (Type_Hi_Lo, mvhi, mvlo);
  or or_4 (EXECUTED, End1, End2, End3, End4, End5, End6, End7, End8, End9);
  or or_5 (Type_AL, add, sub, mult, mulu, div, divu, \and , \or , \nor , \xor , slt, sltu);
  and and_7 (and_7_out, EXCECUTE, Type_Inm_t);
  or or_6 (or_6_out, En_Ram1, En_Ram3, En_Ram4, En_Ram2);
  or or_7 (UseRam, or_6_out, En_Ram);
  assign operation_sel = op_sel_1 | op_sel_2 | op_sel_3;  // OR_Gate or_8, 4 bits wide
  or or_9 (operand_A_sel, operand_A_sel_1, operand_A_sel_2);
  assign operand_B_sel = operand_B_sel_1 | operand_B_sel_2 | operand_B_sel_3 | operand_B_sel_4 | operand_B_sel_5;  // OR_Gate or_10, 2 bits wide
  // TYPE_INM type_inm_1: pin names not known; wires that end beside it: op_sel_2_t, operand_B_SEL1, Ld_Pc2_t, W_RF2, End2
  or or_11 (Type_Inm, addi, andi, andi, xori, slti, sltiu);
  or or_12 (Type_Branch, nop, beq, bne, blez, bgtz, bltz, J, jr);
  or or_13 (Type_Special, Halt, tty_En, rnd, kbd);
  assign Di_Sel = Di_Sel1 | Di_Sel2 | Di_Sel3 | Di_Sel4;  // OR_Gate or_14, 3 bits wide
  or or_15 (WRF, WRF3, WRF6, WRF1, WRF2, WRF5, WRF4);
  or or_16 (WSP, WSp1, WSp2);
  or or_17 (LD_PC, Ld_Pc1, Ld_Pc2, Ld_Pc3, Ld_Pc4, Ld_Pc5, Ld_Pc6, Ld_Pc7, Ld_Pc8, Ld_Pc9);
  assign or_18_out = ADDR_Sel1 | ADDR_Sel2;  // OR_Gate or_18, 2 bits wide
  assign Addres_Sel = or_18_out | ADDR_Sel;  // OR_Gate or_19, 2 bits wide

  // Other names for the same wires on the sheet: clk = in_3; FuncCode[5:0] = in_2; OpCode[5:0] = in_1; ori = andi;
  //   Ram_Rdy = in_4; RESET_EXECUTORS = LD_IR; start = in_5; tty = tty_En; W_Ram = WriteRam
endmodule

module Type_AL (
  input  in_1,
  input  in_2,
  input  in_3,
  input  in_4,
  input  in_5,
  input  in_6,
  input  in_7,
  input  in_8,
  input  in_9,
  input  in_10,
  input  in_11,
  input  in_12,
  input  in_13,
  output [3:0] Operation_Sel,
  output WRF,
  output WH_L,
  output LD_PC,
  output End
);

  wire not_1_out, or_1_out;
  wire [3:0] Operation_Sel_t;

  assign Operation_Sel = Operation_Sel_t & {4{in_13}};  // AND_Gate and_1, 4 bits wide
  or or_1 (or_1_out, in_3, in_4, in_5, in_6);
  Priority_Encoder #(.select(4)) priority_encoder_1 (
    .in0(in_1), .in1(in_2), .in2(in_7), .in3(in_8), .in4(in_9), .in5(in_10), .in6(in_11), .in7(in_12),
    .in8(in_4), .in9(in_3), .in10(in_6), .in11(in_5), .out(Operation_Sel_t));  // open: in12, in13, in14, in15, gs, en_out, en_in
  not not_1 (not_1_out, or_1_out);
  and and_2 (WRF, not_1_out, in_13);
  and and_3 (WH_L, in_13, or_1_out);

  assign End = in_13;
  assign LD_PC = in_13;

  // Other names for the same wires on the sheet: enable = in_13; add = in_1; and = in_7; div = in_5; divu = in_6;
  //   mul = in_3; mulu = in_4; nor = in_9; or = in_8; slt = in_11; sltu = in_12; sub = in_2; xor = in_10
endmodule

module Type_Inmediate (
  input  in_1,
  input  in_2,
  input  in_3,
  input  in_4,
  input  in_5,
  input  in_6,
  input  in_7,
  output [3:0] operand_sel,
  output [1:0] Operand_B,
  output WRF,
  output Pc_LD,
  output \end 
);

  wire or_1_out;

  or or_1 (or_1_out, in_1, in_6);
  and and_1 (Operand_B[1], or_1_out, in_7);
  Priority_Encoder #(.select(4)) priority_encoder_1 (
    .in0(in_1), .in2(in_2), .in3(in_3), .in5(in_4), .in6(in_5), .in7(in_6), .out(operand_sel));  // open: in1, in4, in8, in9, in10, in11, in12, in13, in14, in15, gs, en_out, en_in

  assign \end  = in_7;
  assign Operand_B[0] = in_7;
  assign Pc_LD = in_7;
  assign WRF = in_7;

  // Other names for the same wires on the sheet: addi = in_1; andi = in_2; op_sel[3:0] = operand_sel; enable = in_7;
  //   ori = in_3; slti = in_5; sltiu = in_6; xori = in_4
endmodule

module Branch_Operations (
  input  in_1,
  input  in_2,
  input  in_3,
  input  in_4,
  input  in_5,
  input  in_6,
  input  in_7,
  input  in_8,
  input  in_9,
  output [2:0] Branch_sel,
  output [1:0] Pc_Sel,
  output Ld_PC,
  output \end 
);

  wire not_1_out, not_2_out, not_3_out, not_4_out, not_5_out, not_6_out;
  wire [1:0] and_2_out;
  wire [2:0] Branch_Sel_t;

  Priority_Encoder priority_encoder_1 (
    .in0(in_1), .in1(in_2), .in2(in_4), .in3(in_3), .in4(in_5), .in5(in_8), .out(Branch_Sel_t));  // open: in6, in7, en_in, gs, en_out
  not not_1 (not_1_out, in_1);
  not not_2 (not_2_out, in_2);
  not not_3 (not_3_out, in_3);
  not not_4 (not_4_out, in_4);
  not not_5 (not_5_out, in_5);
  not not_6 (not_6_out, in_6);
  and and_1 (and_2_out[1], not_6_out, in_9);
  and and_2 (and_2_out[0], not_1_out, not_2_out, not_3_out, not_4_out, not_5_out, in_9);
  Multiplexer #(.width(2), .enable("false")) multiplexer_1 (.in0(and_2_out), .in1(2'b00), .out(Pc_Sel), .sel(in_8));
  assign Branch_sel = Branch_Sel_t & {3{in_9}};  // AND_Gate and_3, 3 bits wide

  assign \end  = in_9;
  assign Ld_PC = in_9;

  // Other names for the same wires on the sheet: enable = in_9; Beq = in_1; Bgtz = in_4; Blez = in_3; Bltz = in_5;
  //   Bne = in_2; j = in_6; jr = in_7; nop = in_8
endmodule

module Ram_Handler (
  input  [31:0] in_1,
  input  [31:0] in_2,
  input  [31:0] in_3,
  input  [31:0] in_4,
  input  [31:0] in_5,
  input  in_6,
  input  in_7,
  input  [3:0] Read_Time,
  input  in_9,
  input  in_10,
  input  [3:0] Write_Time,
  output [31:0] Ram_out,
  output [3:0] Output,
  output [15:0] ADDR,
  output RAm_Ready,
  output CS,
  output Output_2
);

  wire comparator_1_lt, d_ff_1_q, demultiplexer_1_out0, demultiplexer_1_out1, IsFetch, or_1_out;
  wire [3:0] counter_1_q, Time;
  wire [31:0] Ram_Out0, Ram_Out1, Ram_Out2, Ram_Out3;

  LE_Mode le_mode_1 (.in_1(in_2), .Output(Ram_Out0));
  LE_Mode le_mode_2 (.in_1(in_3), .Output(Ram_Out1));
  LE_Mode le_mode_3 (.in_1(in_4), .Output(Ram_Out2));
  LE_Mode le_mode_4 (.in_1(in_5), .Output(Ram_Out3));
  Multiplexer #(.width(4), .enable("false")) multiplexer_1 (.in0(Read_Time), .in1(Write_Time), .out(Time), .sel(in_10));
  Counter #(.width(4), .max('hf)) counter_1 (
    .count(CS), .Q(counter_1_q), .clk(in_6), .clr(or_1_out));  // open: load, D, carry
  or or_1 (or_1_out, in_7, RAm_Ready);
  D_Flip_Flop #(.trigger("falling")) d_ff_1 (
    .clk(in_6), .D(demultiplexer_1_out0), .Q(d_ff_1_q));  // open: Qn, preset, en, reset
  or or_2 (CS, d_ff_1_q, in_9);
  Comparator #(.width(4)) comparator_1 (.a(counter_1_q), .b(Time), .lt(comparator_1_lt));  // open: gt, eq
  not not_1 (IsFetch, comparator_1_lt);
  Demultiplexer #(.enable("false")) demultiplexer_1 (
    .out0(demultiplexer_1_out0), .out1(demultiplexer_1_out1), .in(CS), .sel(IsFetch));
  D_Flip_Flop #(.trigger("falling")) d_ff_2 (
    .clk(in_6), .D(demultiplexer_1_out1), .Q(RAm_Ready));  // open: Qn, preset, en, reset
  Decoder #(.select(2), .enable("false")) decoder_1 (
    .out0(Output[0]), .out1(Output[1]), .out2(Output[2]), .out3(Output[3]), .sel(in_1[1:0]));
  Multiplexer #(.select(2), .width(32), .enable("false")) multiplexer_2 (
    .in0(Ram_Out0), .in1(Ram_Out1), .in2(Ram_Out2), .in3(Ram_Out3), .out(Ram_out), .sel(in_1[1:0]));
  and and_1 (Output_2, in_10, CS);

  assign ADDR = in_1[17:2];

  // Other names for the same wires on the sheet: clk = in_6; count = CS; RamWr = CS; Clear = RAm_Ready;
  //   End = RAm_Ready; Bank[1:0] = in_1[1:0]; Block[15:0] = in_1[17:2]; Rst = in_7; Rw = in_10; start = in_9

  // Notes on the sheet:
  //   Address
  //   Data From Ram
  //   Ram Timing
  //   Timer
  //   Flow Control
  //   Control Signals
endmodule

module LE_Mode (
  input  [31:0] in_1,
  output [31:0] Output
);


  assign Output = {in_1[3:0], in_1[7:4], in_1[11:8], in_1[15:12], in_1[19:16], in_1[23:20], in_1[27:24], in_1[31:28]};
endmodule

module Type_H_L (
  input  in_1,
  input  in_2,
  input  in_3,
  output wrf,
  output LD_PC,
  output [2:0] Di_Sel,
  output \end 
);

  Multiplexer #(.width(3)) multiplexer_1 (.in0(3'b001), .in1(3'b010), .out(Di_Sel), .sel(in_1), .en(in_3));

  assign \end  = in_3;
  assign LD_PC = in_3;
  assign wrf = in_3;

  // Other names for the same wires on the sheet: enable = in_3; mvHi = in_1; mvLo = in_2
endmodule

module Pop (
  input  in_1,
  input  in_2,
  input  in_3,
  input  in_4,
  output Operand_B_Sel,
  output Output,
  output [1:0] out_7,
  output [1:0] Operand_A_Sel,
  output Output_2,
  output Output_3,
  output Output_4,
  output [2:0] out_12,
  output Output_5
);

  wire demultiplexer_1_out0, demultiplexer_1_out1, demultiplexer_3_out0, demultiplexer_3_out1, IDLE_q,
       or_1_out, or_2_out, or_3_out, WAIT_q;

  D_Flip_Flop #(.trigger("falling")) IDLE (
    .clk(in_4), .D(demultiplexer_1_out0), .Q(IDLE_q), .preset(in_2));  // open: Qn, en, reset
  Demultiplexer demultiplexer_1 (
    .out0(demultiplexer_1_out0), .out1(demultiplexer_1_out1), .in(or_1_out), .sel(in_2));  // open: en
  or or_1 (or_1_out, IDLE_q, demultiplexer_3_out1);
  or or_2 (or_2_out, Operand_A_Sel[1], demultiplexer_1_out1);
  Demultiplexer demultiplexer_2 (.out0(Operand_A_Sel[1]), .out1(Output), .in(WAIT_q), .sel(in_1));  // open: en
  D_Flip_Flop #(.trigger("falling")) WAIT (.clk(in_4), .D(or_2_out), .Q(WAIT_q));  // open: Qn, preset, en, reset
  or or_3 (or_3_out, demultiplexer_3_out0, Output);
  D_Flip_Flop #(.trigger("falling")) END (.clk(in_4), .D(or_3_out), .Q(Output_5));  // open: Qn, preset, en, reset
  Demultiplexer demultiplexer_3 (
    .out0(demultiplexer_3_out0), .out1(demultiplexer_3_out1), .in(Output_5), .sel(in_3));  // open: en
  Multiplexer #(.width(2), .enable("false")) multiplexer_1 (.in0(2'b00), .in1(2'b01), .out(out_7), .sel(Output));
  Multiplexer #(.width(3), .enable("false")) multiplexer_2 (.in0(3'b000), .in1(3'b011), .out(out_12), .sel(Output));

  assign Operand_A_Sel[0] = Operand_A_Sel[1];
  assign Operand_B_Sel = Operand_A_Sel[1];
  assign Output_2 = Output;
  assign Output_3 = Output;
  assign Output_4 = Output;

  // Other names for the same wires on the sheet: Addr_sel[1:0] = {2{Operand_A_Sel[1]}}; En_Ram = Operand_A_Sel[1];
  //   clk = in_4; enable = in_2; End = Output_5; Di_sel = Output; LD_PC = Output; operand_A_sel_t = Output;
  //   operand_B_sel_t = Output; WRF = Output; WSP = Output; Ram_Rdy = in_1; rst = in_3
endmodule

module Push (
  input  in_1,
  input  in_2,
  input  in_3,
  input  in_4,
  output out_5,
  output out_6,
  output [1:0] out_7,
  output [2:0] out_8,
  output out_9,
  output [1:0] out_10,
  output [3:0] out_11,
  output Output,
  output out_13,
  output out_14
);

  wire demultiplexer_1_out0, demultiplexer_3_out0, demultiplexer_3_out1, IDLE_q, or_1_out, or_2_out,
       or_3_out, undriven, WAIT_q;

  D_Flip_Flop #(.trigger("falling")) IDLE (
    .clk(in_4), .D(demultiplexer_1_out0), .Q(IDLE_q), .preset(in_2));  // open: Qn, en, reset
  Demultiplexer #(.enable("false")) demultiplexer_1 (
    .out0(demultiplexer_1_out0), .out1(out_9), .in(or_1_out), .sel(in_2));
  or or_1 (or_1_out, IDLE_q, demultiplexer_3_out1);
  or or_2 (or_2_out, out_5, out_9);
  D_Flip_Flop #(.trigger("falling")) WAIT (.clk(in_4), .D(or_2_out), .Q(WAIT_q));  // open: Qn, preset, en, reset
  Demultiplexer #(.enable("false")) demultiplexer_2 (.out0(out_5), .out1(out_14), .in(WAIT_q), .sel(in_1));
  Multiplexer #(.width(4), .enable("false")) multiplexer_1 (.in0(4'b0000), .in1(4'b0001), .out(out_11), .sel(out_9));
  Multiplexer #(.width(2), .enable("false")) multiplexer_2 (.in0(2'b00), .in1(2'b01), .out(out_10), .sel(out_9));
  or or_3 (or_3_out, demultiplexer_3_out0, out_14);
  Demultiplexer #(.enable("false")) demultiplexer_3 (
    .out0(demultiplexer_3_out0), .out1(demultiplexer_3_out1), .in(Output), .sel(in_3));
  D_Flip_Flop #(.trigger("falling")) END (
    .clk(in_4), .D(or_3_out), .Q(Output), .reset(undriven));  // open: Qn, preset, en

  assign out_6 = out_5;
  assign out_7 = {2{out_5}};
  assign out_13 = out_9;

  // Other names for the same wires on the sheet: ADDR_SEL[1:0] = {2{out_5}}; en_RAM = out_5; W_RAM = out_5;
  //   CLK = in_4; DI_SEL[2:0] = out_8; enable = in_2; END = Output; LD_PC = out_14; en_operand_B_Selector = out_9;
  //   en_operation_sel = out_9; operand_A_Selector = out_9; W_SP = out_9; RamReady = in_1; RST = in_3
endmodule
